# Fritzing sketch shift_reg (saved by Fritzing 0.9.3b)
breadboards: 1

parts:
  Mod1 = Raspberry Pi Pico
  7_Segment1 = 7 Segment Display
  R1 = Resistor [tolerance=±5% resistance=120 package=THT]
  R2 = Resistor [tolerance=±5% resistance=120 package=THT]
  R3 = Resistor [tolerance=±5% resistance=120 package=THT]
  R4 = Resistor [tolerance=±5% resistance=120 package=THT]
  R5 = Resistor [tolerance=±5% resistance=120 package=THT]
  R6 = Resistor [tolerance=±5% resistance=120 package=THT]
  R7 = Resistor [tolerance=±5% resistance=120 package=THT]
  R8 = Resistor [tolerance=±5% resistance=120 package=THT]
  U1 = 74HC595 [package="DIP16 [THT]"]

nets:
  N1: Mod1.pin_3, Mod1.pin_8, Mod1.pin_13, Mod1.pin_18, Mod1.pin_23, Mod1.pin_28, Mod1.pin_33, Mod1.pin_38, 7_Segment1.common_cathode, U1.GND, U1.OE
  N2: Mod1.pin_9, U1.DS
  N3: Mod1.pin_10, U1.SH_CP
  N4: Mod1.pin_11, U1.ST_CP
  N5: Mod1.pin_12, U1.MR
  N6: Mod1.pin_36, U1.VCC
  N7: 7_Segment1.Segment_E, R3.Pin_1
  N8: 7_Segment1.Segment_D, R6.Pin_1
  N9: 7_Segment1.Segment_C, R5.Pin_0
  N10: 7_Segment1.Segment_DP, R4.Pin_0
  N11: 7_Segment1.Segment_B, R1.Pin_0
  N12: 7_Segment1.Segment_A, R7.Pin_0
  N13: 7_Segment1.Segment_F, R8.Pin_1
  N14: 7_Segment1.Segment_G, R2.Pin_1
  N15: R1.Pin_1, U1.Q1
  N16: R2.Pin_0, U1.Q6
  N17: R3.Pin_0, U1.Q4
  N18: R4.Pin_1, U1.Q7
  N19: R5.Pin_1, U1.Q2
  N20: R6.Pin_0, U1.Q3
  N21: R7.Pin_1, U1.Q0
  N22: R8.Pin_0, U1.Q5

custom parts:
  Raspberry Pi Pico: Raspberry Pi Pico. Based around the RP2040 microcontroller the Pico is a low cost microcontroller device bringing Raspberry Pi quality, cost, and easy of use to the microcontroller space. Jan 2021, Split part in to two versions: tht (this one) and SMD. This one will drill holes for a .1 in header in pcb to allow plugging in the module as well as providing pads to solder the module to the top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
